// Logisim project TrafficLightProject_Logism.circ as structural Verilog: 1 circuit, main circuit main
module main (
  input  B,
  output Y,
  output Z
);

  wire and_1_out, and_2_out, clock_1_out, clock_2_out, d_ff_1_q, d_ff_1_qn, d_ff_2_q, d_ff_2_qn, not_1_out,
       xor_1_out;

  and and_1 (and_1_out, d_ff_2_q, d_ff_1_qn);
  Clock clock_1 (.out(clock_1_out));
  D_Flip_Flop d_ff_1 (.D(and_1_out), .clk(clock_1_out), .Q(d_ff_1_q), .Qn(d_ff_1_qn));  // open: preset, reset
  D_Flip_Flop d_ff_2 (.D(and_2_out), .clk(clock_2_out), .Q(d_ff_2_q), .Qn(d_ff_2_qn));  // open: preset, reset
  and and_2 (and_2_out, xor_1_out, d_ff_1_qn);
  Clock clock_2 (.out(clock_2_out));
  xor xor_1 (xor_1_out, B, d_ff_2_q);
  not not_1 (not_1_out, B);
  and and_3 (Y, not_1_out, d_ff_1_q, d_ff_2_qn);
  and and_4 (Z, d_ff_2_q, d_ff_1_qn);
endmodule
